// Logisim project ex1.circ as structural Verilog: 7 circuits, main circuit main
module main (
  input  [7:0] Input,
  output [7:0] Out2,
  output Out1
);

  not not_1 (Out2[0], Input[0]);
  and and_1 (Out1, Input[0], Input[7]);

  assign Out2[7:1] = Input[7:1];
endmodule

module ExA_2 (
  input  [15:0] Input,
  input  [3:0] in_2,
  output [15:0] Out
);

  wire bitselector_1_out, bitselector_2_out, bitselector_3_out, bitselector_4_out;
  wire [15:0] agiftright2_1_out_3, shiftright4_1_out_3, shiftright8_1_out_3;

  BitSelector #(.width(4)) bitselector_1 (.in(in_2), .out(bitselector_1_out), .sel(2'b11));
  shiftright8 shiftright8_1 (.in_1(Input), .in_2(bitselector_1_out), .out_3(shiftright8_1_out_3));
  BitSelector #(.width(4)) bitselector_2 (.in(in_2), .out(bitselector_2_out), .sel(2'b10));
  shiftright4 shiftright4_1 (.in_1(shiftright8_1_out_3), .in_2(bitselector_2_out), .out_3(shiftright4_1_out_3));
  BitSelector #(.width(4)) bitselector_3 (.in(in_2), .out(bitselector_3_out), .sel(2'b01));
  agiftright2 agiftright2_1 (.in_1(shiftright4_1_out_3), .in_2(bitselector_3_out), .out_3(agiftright2_1_out_3));
  shiftright1 shiftright1_1 (.in_1(agiftright2_1_out_3), .in_2(bitselector_4_out), .out_3(Out));
  BitSelector #(.width(4)) bitselector_4 (.in(in_2), .out(bitselector_4_out), .sel(2'b00));
endmodule

module shiftright4 (
  input  [15:0] in_1,
  input  in_2,
  output [15:0] out_3
);

  BitSelector #(.width(32), .group(16)) bitselector_1 (.in({in_1[3:0], in_1[15:4], in_1}), .out(out_3), .sel(in_2));
endmodule

module shiftright8 (
  input  [15:0] in_1,
  input  in_2,
  output [15:0] out_3
);

  wire [15:0] shiftright4_1_out_3;

  shiftright4 shiftright4_1 (.in_1(in_1), .in_2(in_2), .out_3(shiftright4_1_out_3));
  shiftright4 shiftright4_2 (.in_1(shiftright4_1_out_3), .in_2(in_2), .out_3(out_3));
endmodule

module agiftright2 (
  input  [15:0] in_1,
  input  in_2,
  output [15:0] out_3
);

  wire [15:0] shiftright1_1_out_3;

  shiftright1 shiftright1_1 (.in_1(in_1), .in_2(in_2), .out_3(shiftright1_1_out_3));
  shiftright1 shiftright1_2 (.in_1(shiftright1_1_out_3), .in_2(in_2), .out_3(out_3));
endmodule

module shiftright1 (
  input  [15:0] in_1,
  input  in_2,
  output [15:0] out_3
);

  BitSelector #(.width(32), .group(16)) bitselector_1 (.in({in_1[0], in_1[15:1], in_1}), .out(out_3), .sel(in_2));
endmodule

module A3 (
  input  [15:0] in_1,
  output [15:0] out_2,
  output out_3,
  output out_4
);

  wire clock_1_out, clock_2_out, comparator_1_lt, controlled_buffer_1_out, not_2_out;
  wire [7:0] counter_2_q;
  wire [15:0] adder_1_out, counter_1_q, multiplexer_1_out, register_2_q;

  not not_1 (out_3, controlled_buffer_1_out);
  assign controlled_buffer_1_out = not_2_out ? clock_1_out : 1'bz;  // Controlled_Buffer controlled_buffer_1
  Clock #(.highDuration(2), .lowDuration(2)) clock_1 (.out(clock_1_out));
  Register #(.width(16)) register_1 (.D(multiplexer_1_out), .Q(out_2), .clk(controlled_buffer_1_out));  // open: en, clr
  Multiplexer #(.width(16)) multiplexer_1 (
    .in0(adder_1_out), .in1(16'h1), .out(multiplexer_1_out), .sel(out_4));  // open: en
  Register #(.width(16)) register_2 (.D(adder_1_out), .Q(register_2_q), .clk(out_3));  // open: en, clr
  not not_2 (not_2_out, comparator_1_lt);
  Clock clock_2 (.out(clock_2_out));
  Counter #(.width(16), .max('hffff)) counter_1 (
    .Q(counter_1_q), .clk(clock_2_out));  // open: load, D, count, carry, clr
  Adder #(.width(16)) adder_1 (.a(out_2), .b(register_2_q), .out(adder_1_out));  // open: cin, cout
  Comparator #(.width(16)) comparator_1 (.a(in_1), .b(counter_1_q), .lt(comparator_1_lt));  // open: gt, eq
  // Probe on out_2
  Counter counter_2 (.Q(counter_2_q), .clk(clock_1_out));  // open: load, D, count, carry, clr
  Comparator comparator_2 (.a(counter_2_q), .b({8{1'b0}}), .eq(out_4));  // open: gt, lt

  // Other names for the same wires on the sheet: out[15:0] = out_2
endmodule
