// Logisim project cpu.circ as structural Verilog: 4 circuits, main circuit main
module main (
  input  [15:0] From_Instr_Mem,
  input  clk,
  input  Reset,
  output [15:0] r0,
  output [15:0] r1,
  output [15:0] r2,
  output [15:0] r3,
  output [15:0] Display_0,
  output [15:0] Display_1,
  output [15:0] To_Instr_Mem,
  output [15:0] Data_Mem_Data,
  output [15:0] Data_Mem_Addr,
  output Data_Mem_Write
);

  wire and_1_out, and_2_out, beq, bne, Display, Imm, j, jal, jr, jump_jal, lui, MemToReg, nop, not_1_out,
       not_2_out, not_3_out, or_1_out, RegDst, RegWrite, runalu_1_equal, runalu_1_signed_overflow, \signed ;
  wire [1:0] multiplexer_6_out, multiplexer_7_out, rd, rs, rt;
  wire [3:0] opcode;
  wire [5:0] funct;
  wire [7:0] controlled_buffer_2_out, imm_t;
  wire [11:0] target_address;
  wire [15:0] adder_1_out, adder_2_out, ALU_1, ALU_2, bit_extender_1_out, demultiplexer_1_out0,
       demultiplexer_1_out1, multiplexer_1_out, multiplexer_2_out, multiplexer_3_out, multiplexer_4_out,
       multiplexer_5_out, multiplexer_8_out, multiplexer_9_out, multiplexer_10_out, multiplexer_12_out,
       multiplexer_13_out, offset, RAM, register_2_q, shifter_1_out;

  Register #(.width(16)) register_1 (.D(multiplexer_5_out), .Q(To_Instr_Mem), .clk(clk));  // open: en, clr
  LED led_1 (.in(runalu_1_signed_overflow));
  runALU runalu_1 (
    .X(ALU_1), .Y(ALU_2), .funct(funct[3:0]), .opcode(opcode), .Signed_Overflow(runalu_1_signed_overflow),
    .Result(Data_Mem_Addr), .Equal(runalu_1_equal));
  Adder #(.width(16)) adder_1 (.a(To_Instr_Mem), .b(16'h1), .out(adder_1_out));  // open: cin, cout
  // Probe on opcode
  not not_1 (not_1_out, runalu_1_equal);
  Multiplexer #(.width(16)) multiplexer_1 (
    .in0(adder_1_out), .in1(To_Instr_Mem), .out(multiplexer_1_out), .sel(nop));  // open: en
  Multiplexer #(.width(16)) multiplexer_2 (
    .in0(From_Instr_Mem), .in1({16{1'b0}}), .out(multiplexer_2_out), .sel(or_1_out));  // open: en
  or or_1 (or_1_out, nop, jr, jal, j);
  Control control_1 (
    .opcode(opcode), .RegDst(RegDst), .MemWrite(Data_Mem_Write), .MemToReg(MemToReg), .RegWrite(RegWrite),
    .\signed (\signed ), .Imm(Imm), .jal(jal), .jump_jal(j), .jr(jr), .bne(bne), .beq(beq), .lui(lui),
    .Display(Display));
  and and_1 (and_1_out, not_1_out, bne);
  or or_2 (nop, and_1_out, and_2_out);
  and and_2 (and_2_out, runalu_1_equal, beq);
  Multiplexer #(.width(16)) multiplexer_3 (
    .in0(multiplexer_1_out), .in1(adder_2_out), .out(multiplexer_3_out), .sel(nop));  // open: en
  Adder #(.width(16)) adder_2 (.a(multiplexer_1_out), .b(offset), .out(adder_2_out));  // open: cin, cout
  splitter splitter_1 (
    .clk(register_2_q), .rd(funct), .out_3(rd), .out_4(imm_t), .rt(rt), .rs(rs), .opcode(opcode),
    .target_address(target_address));
  Register #(.width(16)) register_2 (.D(multiplexer_2_out), .Q(register_2_q), .clk(clk));  // open: en, clr
  Multiplexer #(.width(16)) multiplexer_4 (
    .in0(multiplexer_3_out), .in1({To_Instr_Mem[15:12], target_address}), .out(multiplexer_4_out),
    .sel(jump_jal));  // open: en
  Multiplexer #(.width(16)) multiplexer_5 (
    .in0(multiplexer_4_out), .in1(ALU_1), .out(multiplexer_5_out), .sel(jr));  // open: en
  Multiplexer #(.width(2), .enable("false")) multiplexer_6 (.in0(rt), .in1(rd), .out(multiplexer_6_out), .sel(RegDst));
  Multiplexer #(.width(2)) multiplexer_7 (
    .in0(multiplexer_6_out), .in1(2'b11), .out(multiplexer_7_out), .sel(jal));  // open: en
  Multiplexer #(.width(16)) multiplexer_8 (
    .in0(multiplexer_9_out), .in1(To_Instr_Mem), .out(multiplexer_8_out), .sel(jal));  // open: en
  Multiplexer #(.width(16)) multiplexer_9 (
    .in0(multiplexer_10_out), .in1(shifter_1_out), .out(multiplexer_9_out), .sel(lui));  // open: en
  Multiplexer #(.width(16)) multiplexer_10 (
    .in0(Data_Mem_Addr), .in1(RAM), .out(multiplexer_10_out), .sel(MemToReg));  // open: en
  assign RAM = Data_Mem_Write ? Data_Mem_Data : 16'bz;  // Controlled_Buffer controlled_buffer_1
  not not_2 (not_2_out, Data_Mem_Write);
  RAM #(.addrWidth(16), .dataWidth(16)) ram_1 (
    .addr(Data_Mem_Addr), .data(RAM), .sel(1'b1), .clk(clk), .ld(not_2_out), .clr(Reset));
  Regfile_main main_1 (
    .Read_register_1(rs), .Read_register_2(rt), .write_register(multiplexer_7_out),
    .write_data(multiplexer_8_out), .Reg_0_Value(r0), .Reg_1_Value(r1), .Reg_2_Value(r2), .Reg_3_Value(r3),
    .RegWrite(RegWrite), .clock(clk), .Read_Data_1(ALU_1), .Read_Data_2(Data_Mem_Data));
  Multiplexer #(.width(16)) multiplexer_11 (
    .in0(Data_Mem_Data), .in1(multiplexer_12_out), .out(ALU_2), .sel(Imm));  // open: en
  Shifter #(.width(16)) shifter_1 (.in(multiplexer_12_out), .\dist (4'b1000), .out(shifter_1_out));
  assign bit_extender_1_out = {{8{1'b0}}, imm_t};  // Bit_Extender bit_extender_1
  assign offset = {{8{imm_t[7]}}, imm_t};  // Bit_Extender bit_extender_2
  Multiplexer #(.width(16)) multiplexer_12 (
    .in0(bit_extender_1_out), .in1(offset), .out(multiplexer_12_out), .sel(\signed ));  // open: en
  assign controlled_buffer_2_out = Display ? imm_t : 8'bz;  // Controlled_Buffer controlled_buffer_2
  Multiplexer #(.width(16)) multiplexer_13 (
    .in0({16{1'b0}}), .in1(ALU_1), .out(multiplexer_13_out), .sel(Display));  // open: en
  Demultiplexer #(.width(16), .enable("false")) demultiplexer_1 (
    .out0(demultiplexer_1_out0), .out1(demultiplexer_1_out1), .in(multiplexer_13_out),
    .sel(controlled_buffer_2_out[0]));
  not not_3 (not_3_out, controlled_buffer_2_out[0]);
  Hex_Digit_Display hex_digit_display_1 (.value(Display_0[15:12]));  // open: dp
  Hex_Digit_Display hex_digit_display_2 (.value(Display_0[11:8]));  // open: dp
  Hex_Digit_Display hex_digit_display_3 (.value(Display_0[3:0]));  // open: dp
  Hex_Digit_Display hex_digit_display_4 (.value(Display_0[7:4]));  // open: dp
  Register #(.width(16)) register_3 (.D(demultiplexer_1_out0), .en(not_3_out), .Q(Display_0), .clk(clk));  // open: clr
  Hex_Digit_Display hex_digit_display_5 (.value(Display_1[15:12]));  // open: dp
  Hex_Digit_Display hex_digit_display_6 (.value(Display_1[11:8]));  // open: dp
  Hex_Digit_Display hex_digit_display_7 (.value(Display_1[7:4]));  // open: dp
  Register #(.width(16)) register_4 (
    .D(demultiplexer_1_out1), .en(controlled_buffer_2_out[0]), .Q(Display_1), .clk(clk));  // open: clr
  Hex_Digit_Display hex_digit_display_8 (.value(Display_1[3:0]));  // open: dp

  // Other names for the same wires on the sheet: ALUOut[15:0] = Data_Mem_Addr; Curr_PC[15:0] = To_Instr_Mem;
  //   d0[15:0] = Display_0; d1[15:0] = Display_1; MemWrite = Data_Mem_Write; rtval[15:0] = Data_Mem_Data

  // Notes on the sheet:
  //   This is the current PC that you need to send as OUTPUT
  //   This is the instruction that you would receive as INPUT
  //   This is a CLK that is an INPUT driven from the harness.
  //   Remember, this circuit is loaded from the harness to be tested!
  //   DO NOT CHANGE THE LOCATIONS OF THE INPUTS OR OUTPUTS! IF YOU DO SO, YOU NEED TO MAKE SURE THE PINS ARE IN THE RIGHT PLACES!
  //   These are OUTPUTS of the circuit
  //   These are OUTPUTS to the circuit
endmodule

module splitter (
  input  [15:0] clk,
  output [5:0] rd,
  output [1:0] out_3,
  output [7:0] out_4,
  output [1:0] rt,
  output [1:0] rs,
  output [3:0] opcode,
  output [11:0] target_address
);


  assign opcode = clk[15:12];
  assign out_3 = clk[7:6];
  assign out_4 = clk[7:0];
  assign rd = clk[5:0];
  assign rs = clk[11:10];
  assign rt = clk[9:8];
  assign target_address = clk[11:0];

  // Notes on the sheet:
  //   Funct
endmodule

module runALU (
  input  [15:0] X,
  input  [15:0] Y,
  input  [3:0] funct,
  input  [3:0] opcode,
  output Signed_Overflow,
  output [15:0] Result,
  output Equal
);

  wire [3:0] multiplexer_1_out, multiplexer_2_out;

  Multiplexer #(.select(4), .width(4)) multiplexer_1 (
    .in0(4'b0000), .in1(4'b0001), .in2(4'b0010), .in3(4'b0011), .in4(4'b0100), .in5(4'b0101), .in6(4'b0110),
    .in7(4'b0111), .in8(4'b1000), .in9(4'b1001), .out(multiplexer_1_out), .sel(funct));  // open: in10, in11, in12, in13, in14, in15, en
  Multiplexer #(.select(4), .width(4)) multiplexer_2 (
    .in0(multiplexer_1_out), .in5(4'b0000), .in6(4'b0111), .in7(4'b0110), .in10(4'b0010), .in12(4'b0110),
    .in14(4'b0110), .out(multiplexer_2_out), .sel(opcode));  // open: in1, in2, in3, in4, in8, in9, in11, in13, in15, en
  alu_main main_1 (
    .Switch__S(multiplexer_2_out), .X(X), .Equal(Equal), .RESULT(Result), .Signed_Overflow(Signed_Overflow),
    .Y(Y));
endmodule

module Control (
  input  [3:0] opcode,
  output RegDst,
  output MemWrite,
  output MemToReg,
  output RegWrite,
  output \signed ,
  output Imm,
  output jal,
  output jump_jal,
  output jr,
  output bne,
  output beq,
  output lui,
  output Display
);

  wire [15:13] multiplexer_1_out;

  // Probe on 16'h9
  // Probe on 16'h80
  // Probe on {multiplexer_1_out, Display, lui, beq, bne, jr, jump_jal, jal, Imm, \signed , RegWrite, MemToReg, MemWrite, RegDst}
  Multiplexer #(.select(4), .width(16), .enable("false")) multiplexer_1 (
    .in0(16'h9), .in1(16'h80), .in2(16'h100), .in3(16'h100), .in4(16'h400), .in5(16'h28), .in6(16'h28),
    .in7(16'h380), .in8(16'h200), .in9(16'h32), .in10(16'h828), .in11(16'h3c), .in12(16'h1000),
    .out({multiplexer_1_out, Display, lui, beq, bne, jr, jump_jal, jal, Imm, \signed , RegWrite, MemToReg, MemWrite, RegDst}),
    .sel(opcode));  // open: in13, in14, in15

  // Notes on the sheet:
  //   1
  //   2
  //   3
  //   4
  //   5
  //   6
  //   7
  //   8
  //   9
  //   10
  //   11
  //   12
  //   13
endmodule
