// Logisim project alu.circ as structural Verilog: 7 circuits, main circuit main
module main (
  input  [15:0] X,
  input  [15:0] Y,
  input  [3:0] Switch__S,
  output Signed_Overflow,
  output [15:0] RESULT,
  output Equal
);

  wire add8p_2_overflow, add16overflow_1_out, comparator_1_lt, sub8p_2_overflow, sub16overflow_1_out;
  wire [15:0] add8p_1_out, adder_1_out, and_out, multiplexer_1_out, or_out, shifter_1_out, shifter_2_out,
       shifter_3_out, sub8p_1_out, subtractor_1_out, X_t, Y_t;

  // Probe on Switch__S
  Comparator #(.width(16)) comparator_1 (.a(X_t), .b(Y_t), .lt(comparator_1_lt));  // open: gt, eq
  Adder #(.width(16)) adder_1 (.a(X), .b(Y), .out(adder_1_out));  // open: cin, cout
  Subtractor #(.width(16)) subtractor_1 (.a(X), .b(Y), .out(subtractor_1_out));  // open: bin, bout
  Shifter #(.width(16)) shifter_1 (.in(X), .\dist (Y[3:0]), .out(shifter_1_out));
  Shifter #(.width(16), .shift("lr")) shifter_2 (.in(X), .\dist (Y[3:0]), .out(shifter_2_out));
  Shifter #(.width(16), .shift("ar")) shifter_3 (.\dist (Y[3:0]), .out(shifter_3_out));  // open: in
  Multiplexer #(.width(16)) multiplexer_1 (
    .in0({16{1'b0}}), .in1(16'h1), .out(multiplexer_1_out), .sel(comparator_1_lt));  // open: en
  assign or_out = X | Y;  // OR_Gate or, 16 bits wide
  assign and_out = X & Y;  // AND_Gate and, 16 bits wide
  add8p add8p_1 (.in_1(X), .Y(Y), .out(add8p_1_out));  // open: Overflow
  sub8p sub8p_1 (.in_1(X), .Y(Y), .out(sub8p_1_out));  // open: Overflow
  Multiplexer #(.select(4), .width(16)) multiplexer_2 (
    .in0(adder_1_out), .in1(subtractor_1_out), .in2(shifter_1_out), .in3(shifter_2_out), .in4(shifter_3_out),
    .in5(multiplexer_1_out), .in6(or_out), .in7(and_out), .in8(add8p_1_out), .in9(sub8p_1_out), .out(RESULT),
    .sel(Switch__S));  // open: in10, in11, in12, in13, in14, in15, en
  // Probe on Switch__S
  add16overflow add16overflow_1 (.in_1(X), .Y(Y), .out(add16overflow_1_out));
  sub16overflow sub16overflow_1 (.in_1(X), .Y(Y), .out(sub16overflow_1_out));
  add8p add8p_2 (.in_1(X), .Y(Y), .Overflow(add8p_2_overflow));  // open: out
  sub8p sub8p_2 (.in_1(X), .Y(Y), .Overflow(sub8p_2_overflow));  // open: out
  Multiplexer #(.select(4)) multiplexer_3 (
    .in0(add16overflow_1_out), .in1(sub16overflow_1_out), .in8(add8p_2_overflow), .in9(sub8p_2_overflow),
    .out(Signed_Overflow), .sel(Switch__S));  // open: in2, in3, in4, in5, in6, in7, in10, in11, in12, in13, in14, in15, en
  Comparator #(.width(16)) comparator_2 (.a(X), .b(Y), .eq(Equal));  // open: gt, lt

  // Other names for the same wires on the sheet: SWITCH[3:0] = Switch__S; y_0_3[3:0] = Y[3:0]

  // Notes on the sheet:
  //   INPUTS to your circuit
  //   INPUT to your circuit
  //   DON'T CHANGE THE INPUTS AND OUTPUTS! IF YOU DO SO, YOU NEED TO MAKE SURE THE PINS ARE IN THE RIGHT PLACES!
  //   OUTPUTS of your circuit
endmodule

module add16overflow (
  input  [15:0] in_1,
  input  [15:0] Y,
  output out
);

  wire and_1_out, and_2_out, not_1_out, not_2_out, not_3_out;
  wire [15:0] adder_1_out, adder_2_out;

  not not_1 (not_1_out, adder_1_out[15]);
  Adder #(.width(16)) adder_1 (.a(Y), .b(in_1), .out(adder_1_out));  // open: cin, cout
  not not_2 (not_2_out, in_1[15]);
  not not_3 (not_3_out, Y[15]);
  Adder #(.width(16)) adder_2 (.a(Y), .b(in_1), .out(adder_2_out));  // open: cin, cout
  and and_1 (and_1_out, in_1[15], not_1_out, Y[15]);
  and and_2 (and_2_out, not_2_out, adder_2_out[15], not_3_out);
  or or_1 (out, and_1_out, and_2_out);

  // Other names for the same wires on the sheet: x[15:0] = in_1
endmodule

module sub16overflow (
  input  [15:0] in_1,
  input  [15:0] Y,
  output out
);

  wire and_1_out, and_2_out, not_1_out, not_2_out, not_3_out;
  wire [15:0] subtractor_1_out, subtractor_2_out;

  // Probe on in_1
  not not_1 (not_1_out, in_1[15]);
  Subtractor #(.width(16)) subtractor_1 (.a(in_1), .b(Y), .out(subtractor_1_out));  // open: bin, bout
  not not_2 (not_2_out, Y[15]);
  Subtractor #(.width(16)) subtractor_2 (.a(in_1), .b(Y), .out(subtractor_2_out));  // open: bin, bout
  // Probe on subtractor_1_out
  not not_3 (not_3_out, subtractor_2_out[15]);
  and and_1 (and_1_out, not_1_out, Y[15], subtractor_1_out[15]);
  and and_2 (and_2_out, in_1[15], not_2_out, not_3_out);
  or or_1 (out, and_1_out, and_2_out);

  // Other names for the same wires on the sheet: x[15:0] = in_1
endmodule

module add8overflow (
  input  [7:0] in_1,
  input  [7:0] in_2,
  output out
);

  wire and_1_out, and_2_out, not_1_out, not_2_out, not_3_out;
  wire [7:0] adder_1_out, adder_2_out;

  not not_1 (not_1_out, adder_1_out[7]);
  Adder adder_1 (.a(in_2), .b(in_1), .out(adder_1_out));  // open: cin, cout
  not not_2 (not_2_out, in_1[7]);
  not not_3 (not_3_out, in_2[7]);
  Adder adder_2 (.a(in_2), .b(in_1), .out(adder_2_out));  // open: cin, cout
  and and_1 (and_1_out, in_1[7], not_1_out, in_2[7]);
  and and_2 (and_2_out, not_2_out, adder_2_out[7], not_3_out);
  or or_1 (out, and_1_out, and_2_out);

  // Other names for the same wires on the sheet: x[7:0] = in_1; y[7:0] = in_2

  // Notes on the sheet:
  //   Negative
  //   Positive
  //   sum of two negative is positive
  //   sum of two positive is negative
endmodule

module sub8overflow (
  input  [7:0] in_1,
  input  [7:0] in_2,
  output out
);

  wire and_1_out, and_2_out, not_1_out, not_2_out, not_3_out;
  wire [7:0] subtractor_1_out, subtractor_2_out;

  // Probe on in_1
  not not_1 (not_1_out, in_1[7]);
  Subtractor subtractor_1 (.a(in_1), .b(in_2), .out(subtractor_1_out));  // open: bin, bout
  not not_2 (not_2_out, in_2[7]);
  Subtractor subtractor_2 (.a(in_1), .b(in_2), .out(subtractor_2_out));  // open: bin, bout
  // Probe on subtractor_1_out
  not not_3 (not_3_out, subtractor_2_out[7]);
  and and_1 (and_1_out, not_1_out, in_2[7], subtractor_1_out[7]);
  and and_2 (and_2_out, in_1[7], not_2_out, not_3_out);
  or or_1 (out, and_1_out, and_2_out);

  // Other names for the same wires on the sheet: x[7:0] = in_1; y[7:0] = in_2
endmodule

module add8p (
  input  [15:0] in_1,
  input  [15:0] Y,
  output [15:0] out,
  output Overflow
);

  wire add8overflow_1_out, add8overflow_2_out, lowerOverflow2, signedOverflow2, upperOverflow2;

  Adder adder_1 (.a(in_1[7:0]), .b(Y[7:0]), .out(out[7:0]));  // open: cin, cout
  Adder adder_2 (.a(in_1[15:8]), .b(Y[15:8]), .out(out[15:8]));  // open: cin, cout
  add8overflow add8overflow_1 (.in_1(in_1[7:0]), .in_2(Y[7:0]), .out(add8overflow_1_out));
  add8overflow add8overflow_2 (.in_1(in_1[15:8]), .in_2(Y[15:8]), .out(add8overflow_2_out));
  or or_1 (Overflow, add8overflow_1_out, add8overflow_2_out);
  or or_2 (signedOverflow2, lowerOverflow2, upperOverflow2);

  // Other names for the same wires on the sheet: x[15:0] = in_1; x1[7:0] = in_1[7:0]; x0[7:0] = in_1[15:8];
  //   y1[7:0] = Y[7:0]; y0[7:0] = Y[15:8]
endmodule

module sub8p (
  input  [15:0] in_1,
  input  [15:0] Y,
  output [15:0] out,
  output Overflow
);

  wire lowerOverflow2, signedOverflow2, sub8overflow_1_out, sub8overflow_2_out, upperOverflow2;

  Subtractor subtractor_1 (.a(in_1[7:0]), .b(Y[7:0]), .out(out[7:0]));  // open: bin, bout
  Subtractor subtractor_2 (.a(in_1[15:8]), .b(Y[15:8]), .out(out[15:8]));  // open: bin, bout
  sub8overflow sub8overflow_1 (.in_1(in_1[7:0]), .in_2(Y[7:0]), .out(sub8overflow_1_out));
  sub8overflow sub8overflow_2 (.in_1(in_1[15:8]), .in_2(Y[15:8]), .out(sub8overflow_2_out));
  or or_1 (Overflow, sub8overflow_1_out, sub8overflow_2_out);
  or or_2 (signedOverflow2, lowerOverflow2, upperOverflow2);

  // Other names for the same wires on the sheet: x[15:0] = in_1; x1[7:0] = in_1[7:0]; x0[7:0] = in_1[15:8];
  //   y1[7:0] = Y[7:0]; y0[7:0] = Y[15:8]
endmodule
