// Logisim project Regfile.circ as structural Verilog: 1 circuit, main circuit main
module main (
  input  [1:0] Read_register_1,
  input  [1:0] Read_register_2,
  input  [1:0] write_register,
  input  [15:0] write_data,
  input  RegWrite,
  input  clock,
  output [15:0] Reg_0_Value,
  output [15:0] Reg_1_Value,
  output [15:0] Reg_2_Value,
  output [15:0] Reg_3_Value,
  output [15:0] Read_Data_1,
  output [15:0] Read_Data_2
);

  wire demultiplexer_2_out0, demultiplexer_2_out1, demultiplexer_2_out2, demultiplexer_2_out3;
  wire [15:0] temp0, temp1, temp2, temp3;

  Demultiplexer #(.select(2), .width(16)) demultiplexer_1 (
    .out0(temp0), .out1(temp1), .out2(temp2), .out3(temp3), .in(write_data), .sel(write_register),
    .en(RegWrite));
  Register #(.width(16)) register_1 (.D(temp0), .en(demultiplexer_2_out0), .Q(Reg_0_Value), .clk(clock));  // open: clr
  Register #(.width(16)) register_2 (.D(temp1), .en(demultiplexer_2_out1), .Q(Reg_1_Value), .clk(clock));  // open: clr
  // Probe on demultiplexer_2_out1
  // Probe on temp0
  // Probe on temp1
  // Probe on temp3
  Demultiplexer #(.select(2)) demultiplexer_2 (
    .out0(demultiplexer_2_out0), .out1(demultiplexer_2_out1), .out2(demultiplexer_2_out2),
    .out3(demultiplexer_2_out3), .in(1'b1), .sel(write_register));  // open: en
  // Probe on temp2
  Register #(.width(16)) register_3 (.D(temp2), .en(demultiplexer_2_out2), .Q(Reg_2_Value), .clk(clock));  // open: clr
  Register #(.width(16)) register_4 (.D(temp3), .en(demultiplexer_2_out3), .Q(Reg_3_Value), .clk(clock));  // open: clr
  Multiplexer #(.select(2), .width(16)) multiplexer_1 (
    .in0(Reg_0_Value), .in1(Reg_1_Value), .in2(Reg_2_Value), .in3(Reg_3_Value), .out(Read_Data_1),
    .sel(Read_register_1));  // open: en
  Multiplexer #(.select(2), .width(16)) multiplexer_2 (
    .in0(Reg_0_Value), .in1(Reg_1_Value), .in2(Reg_2_Value), .in3(Reg_3_Value), .out(Read_Data_2),
    .sel(Read_register_2));  // open: en

  // Other names for the same wires on the sheet: _0[15:0] = Reg_0_Value; _1[15:0] = Reg_1_Value;
  //   _2[15:0] = Reg_2_Value; _3[15:0] = Reg_3_Value; clk = clock; Read_Reg_1[1:0] = Read_register_1;
  //   Read_Reg_2[1:0] = Read_register_2; WriteToReg[1:0] = write_register

  // Notes on the sheet:
  //   These are INPUTS to the circuit
  //   These are INPUTS to the circuit
  //   DO NOT CHANGE THE LOCATIONS OF THE INPUTS/OUTPUTS! IF YOU DO SO, YOU NEED TO MAKE SURE THE PINS ARE AT THE RIGHT PLACE!
  //   These are OUTPUTS to the circuit
  //   Yet again, the clock is not an actual clock, but an input, one that will be driven from a higher circuit
  //   These are OUTPUTS to the circuit
endmodule
