// Logisim project cpu.circ as structural Verilog: 1 circuit, main circuit main
module main (
  input  [15:0] From_Instr_Mem,
  input  clk,
  input  in_3,
  output [15:0] r0,
  output [15:0] r1,
  output [15:0] r2,
  output [15:0] r3,
  output [15:0] Display_0,
  output [15:0] Display_1,
  output [15:0] To_Instr_Mem,
  output [15:0] Data_Mem_Data,
  output [15:0] Data_Mem_Addr,
  output Data_Mem_Write
);

  wire and_1_out, and_2_out, beq, bne, Display, Imm, jal, jr, jump_jal, kill, lui, main_1_equal,
       main_1_signed_overflow, MemToReg, not_1_out, not_2_out, not_3_out, or_1_out, RegDst, RegWrite,
       \signed ;
  wire [1:0] multiplexer_5_out, multiplexer_6_out, rs, rt;
  wire [3:0] multiplexer_1_out, multiplexer_3_out, opcode;
  wire [5:0] funct;
  wire [7:0] controlled_buffer_1_out;
  wire [7:6] imm_t;
  wire [15:0] adder_1_out, adder_2_out, ALU_1, ALU_2, bit_extender_1_out, demultiplexer_1_out0, disp2, ext,
       multiplexer_2_out, multiplexer_7_out, multiplexer_8_out, multiplexer_9_out, multiplexer_10_out,
       multiplexer_11_out, multiplexer_13_out, multiplexer_16_out, offset, RAM, shifter_1_out, tail;
  wire [15:13] multiplexer_4_out;

  Multiplexer #(.select(4), .width(4)) multiplexer_1 (
    .in0(4'b0000), .in1(4'b0001), .in2(4'b0010), .in3(4'b0011), .in4(4'b0100), .in5(4'b0101), .in6(4'b0110),
    .in7(4'b0111), .in8(4'b1000), .in9(4'b1001), .out(multiplexer_1_out), .sel(funct[3:0]));  // open: in10, in11, in12, in13, in14, in15, en
  or or_1 (or_1_out, jump_jal, jr, jal, kill);
  Multiplexer #(.width(16)) multiplexer_2 (
    .in0(From_Instr_Mem), .in1(16'h6), .out(multiplexer_2_out), .sel(or_1_out));  // open: en
  Register #(.width(16)) register_1 (
    .D(multiplexer_2_out), .Q({opcode, rs, rt, imm_t, funct}), .clk(clk));  // open: en, clr
  // Probe on 16'h9
  Multiplexer #(.select(4), .width(4)) multiplexer_3 (
    .in0(multiplexer_1_out), .in1(4'b0000), .in2(4'b0000), .in3(4'b0000), .in4(4'b0000), .in5(4'b0000),
    .in6(4'b0111), .in7(4'b0110), .in8(4'b0000), .in9(4'b0000), .in10(4'b0000), .in11(4'b0000),
    .in12(4'b0000), .in13(4'b0000), .in14(4'b0000), .in15(4'b0000), .out(multiplexer_3_out), .sel(opcode));  // open: en
  // Probe on 16'hc8
  // Probe on {multiplexer_4_out, Display, lui, beq, bne, jr, jump_jal, jal, Imm, \signed , RegWrite, MemToReg, Data_Mem_Write, RegDst}
  Multiplexer #(.select(4), .width(16), .enable("false")) multiplexer_4 (
    .in0(16'h9), .in1(16'hc8), .in2(16'h80), .in3(16'h100), .in4(16'h400), .in5(16'h38), .in6(16'h28),
    .in7(16'h28), .in8(16'h200), .in9(16'h32), .in10(16'h828), .in11(16'h3c), .in12(16'h1000),
    .out({multiplexer_4_out, Display, lui, beq, bne, jr, jump_jal, jal, Imm, \signed , RegWrite, MemToReg, Data_Mem_Write, RegDst}),
    .sel(opcode));  // open: in13, in14, in15
  // Probe on opcode
  alu_main main_1 (
    .Switch__S(multiplexer_3_out), .X(ALU_1), .Equal(main_1_equal), .RESULT(Data_Mem_Addr),
    .Signed_Overflow(main_1_signed_overflow), .Y(ALU_2));
  LED led_1 (.in(main_1_signed_overflow));
  not not_1 (not_1_out, main_1_equal);
  and and_1 (and_1_out, not_1_out, bne);
  or or_2 (kill, and_1_out, and_2_out);
  and and_2 (and_2_out, main_1_equal, beq);
  Multiplexer #(.width(2), .enable("false")) multiplexer_5 (
    .in0(rt), .in1(imm_t), .out(multiplexer_5_out), .sel(RegDst));
  Register #(.width(16)) register_2 (.D(tail), .Q(To_Instr_Mem), .clk(clk));  // open: en, clr
  Multiplexer #(.width(2)) multiplexer_6 (
    .in0(multiplexer_5_out), .in1(2'b11), .out(multiplexer_6_out), .sel(jal));  // open: en
  Multiplexer #(.width(16)) multiplexer_7 (
    .in0(multiplexer_8_out), .in1(To_Instr_Mem), .out(multiplexer_7_out), .sel(jal));  // open: en
  Multiplexer #(.width(16)) multiplexer_8 (
    .in0(multiplexer_9_out), .in1(shifter_1_out), .out(multiplexer_8_out), .sel(lui));  // open: en
  Multiplexer #(.width(16)) multiplexer_9 (
    .in0(Data_Mem_Addr), .in1(RAM), .out(multiplexer_9_out), .sel(MemToReg));  // open: en
  Adder #(.width(16)) adder_1 (.a(To_Instr_Mem), .b(16'h1), .out(adder_1_out));  // open: cin, cout
  Multiplexer #(.width(16)) multiplexer_10 (
    .in0(adder_1_out), .in1(To_Instr_Mem), .out(multiplexer_10_out), .sel(kill));  // open: en
  Adder #(.width(16)) adder_2 (.a(multiplexer_10_out), .b(offset), .out(adder_2_out));  // open: cin, cout
  Regfile_main main_2 (
    .Read_register_1(rs), .Read_register_2(rt), .write_register(multiplexer_6_out),
    .write_data(multiplexer_7_out), .Reg_0_Value(r0), .Reg_1_Value(r1), .Reg_2_Value(r2), .Reg_3_Value(r3),
    .RegWrite(RegWrite), .clock(clk), .Read_Data_1(ALU_1), .Read_Data_2(Data_Mem_Data));
  Multiplexer #(.width(16)) multiplexer_11 (
    .in0(multiplexer_10_out), .in1(adder_2_out), .out(multiplexer_11_out), .sel(kill));  // open: en
  Multiplexer #(.width(16)) multiplexer_12 (.in0(Data_Mem_Data), .in1(ext), .out(ALU_2), .sel(Imm));  // open: en
  Shifter #(.width(16)) shifter_1 (.in(ext), .\dist (4'b1000), .out(shifter_1_out));
  Multiplexer #(.width(16)) multiplexer_13 (
    .in0(multiplexer_11_out), .in1({To_Instr_Mem[15:12], rs, rt, imm_t, funct}), .out(multiplexer_13_out),
    .sel(jump_jal));  // open: en
  assign bit_extender_1_out = {{8{1'b0}}, {imm_t, funct}};  // Bit_Extender bit_extender_1
  assign offset = {{8{imm_t[7]}}, {imm_t, funct}};  // Bit_Extender bit_extender_2
  assign controlled_buffer_1_out = Display ? {imm_t, funct} : 8'bz;  // Controlled_Buffer controlled_buffer_1
  Multiplexer #(.width(16)) multiplexer_14 (.in0(multiplexer_13_out), .in1(ALU_1), .out(tail), .sel(jr));  // open: en
  Multiplexer #(.width(16)) multiplexer_15 (
    .in0(bit_extender_1_out), .in1(offset), .out(ext), .sel(\signed ));  // open: en
  Multiplexer #(.width(16)) multiplexer_16 (
    .in0({16{1'b0}}), .in1(ALU_1), .out(multiplexer_16_out), .sel(Display));  // open: en
  Demultiplexer #(.width(16), .enable("false")) demultiplexer_1 (
    .out0(demultiplexer_1_out0), .out1(disp2), .in(multiplexer_16_out), .sel(controlled_buffer_1_out[0]));
  not not_2 (not_2_out, Data_Mem_Write);
  not not_3 (not_3_out, controlled_buffer_1_out[0]);
  RAM #(.addrWidth(16), .dataWidth(16)) ram_1 (
    .addr(Data_Mem_Addr), .data(RAM), .sel(1'b1), .clk(clk), .ld(not_2_out), .clr(in_3));
  assign RAM = Data_Mem_Write ? Data_Mem_Data : 16'bz;  // Controlled_Buffer controlled_buffer_2
  Hex_Digit_Display hex_digit_display_1 (.value(Display_0[15:12]));  // open: dp
  Hex_Digit_Display hex_digit_display_2 (.value(Display_0[11:8]));  // open: dp
  Hex_Digit_Display hex_digit_display_3 (.value(Display_0[7:4]));  // open: dp
  Hex_Digit_Display hex_digit_display_4 (.value(Display_0[3:0]));  // open: dp
  Register #(.width(16)) register_3 (.D(demultiplexer_1_out0), .en(not_3_out), .Q(Display_0), .clk(clk));  // open: clr
  Hex_Digit_Display hex_digit_display_5 (.value(Display_1[15:12]));  // open: dp
  Hex_Digit_Display hex_digit_display_6 (.value(Display_1[7:4]));  // open: dp
  Hex_Digit_Display hex_digit_display_7 (.value(Display_1[11:8]));  // open: dp
  Register #(.width(16)) register_4 (
    .D(disp2), .en(controlled_buffer_1_out[0]), .Q(Display_1), .clk(clk));  // open: clr
  Hex_Digit_Display hex_digit_display_8 (.value(Display_1[3:0]));  // open: dp

  // Other names for the same wires on the sheet: MemWrite = Data_Mem_Write; imm_t[5:0] = funct;
  //   target_address[11:0] = {rs, rt, imm_t, funct}; rd[1:0] = imm_t; aluo[15:0] = Data_Mem_Addr;
  //   Curr_PC[15:0] = To_Instr_Mem; d0[15:0] = Display_0; d1[15:0] = Display_1; rtval[15:0] = Data_Mem_Data

  // Notes on the sheet:
  //   0
  //   1
  //   2
  //   3
  //   4
  //   5
  //   6
  //   7
  //   8
  //   9
  //   10
  //   11
  //   12
  //   0
  //   jal
  //   j
  //   jr
  //   beq
  //   addi
  //   andi
  //   ori
  //   bne
  //   sw
  //   lui
  //   lw
  //   disp
  //   This is the current PC that you need to send as OUTPUT
  //   This is the instruction that you would receive as INPUT
  //   Remember, this circuit is loaded from the harness to be tested!
  //   This is a CLK that is an INPUT driven from the harness.
  //   DO NOT CHANGE THE LOCATIONS OF THE INPUTS/OUTPUTS! IF YOU DO SO, YOU NEED TO MAKE SURE THE PINS ARE AT THE RIGHT PLACE!
  //   These are OUTPUTS to the circuit
endmodule
